# Fritzing sketch valve-controller (saved by Fritzing 0.9.10b)
circuit board: 8.46667cm x 5.64444cm
perfboards: 1

parts:
  Part1 = Arduino Nano (Rev3.0)
  J1 = female pin header, 15 pins [form="♀ (female)"]
  J2 = female pin header, 15 pins [form="♀ (female)"]
  LED1 = LED - 5mm [color="Orange (620nm)" current=0.030 package="5 mm [THT]"]
  LED2 = LED - 5mm [color="Orange (620nm)" current=0.030 package="5 mm [THT]"]
  LED3 = LED - 5mm [color="Orange (620nm)" current=0.030 package="5 mm [THT]"]
  LED4 = LED - 5mm [color="Orange (620nm)" current=0.030 package="5 mm [THT]"]
  LED5 = LED - 5mm [color="Orange (620nm)" current=0.030 package="5 mm [THT]"]
  R1 = Resistor [tolerance=±5% power=0.25 resistance=220 package=THT]
  R2 = Resistor [tolerance=±5% power=0.25 resistance=220 package=THT]
  R4 = Resistor [tolerance=±5% power=0.25 resistance=220 package=THT]
  R5 = Resistor [tolerance=±5% power=0.25 resistance=220 package=THT]
  Q1 = Basic FET N-Channel [package="TO220 [THT]"]
  Q2 = Basic FET N-Channel [package="TO220 [THT]"]
  Q3 = Basic FET N-Channel [package="TO220 [THT]"]
  Q4 = Basic FET N-Channel [package="TO220 [THT]"]
  Q5 = Basic FET N-Channel [package="TO220 [THT]"]
  J5 = Camdenboss CTB0158-5 [part_number=CTB0158-5 package=THT]
  J6 = Camdenboss CTB0158-2 [part_number=CTB0158-2 package=THT]
  R3 = Resistor [tolerance=±5% power=0.25 resistance=220 package=THT]

nets:
  N1: Part1.D1/TX, J2.pin15
  N2: Part1.D0/RX, J2.pin14
  N3: Part1.RESET, J1.pin13, J2.pin13
  N4: Part1.GND, J1.pin14, J2.pin12, LED1.cathode, LED2.cathode, LED3.cathode, LED4.cathode, LED5.cathode, Q1.source, Q2.source, Q3.source, Q4.source, Q5.source, J6.pin1
  N5: Part1.D2, J2.pin11, R1.Pin_0, Q1.gate
  N6: Part1.D3, J2.pin10, R4.Pin_0, Q2.gate
  N7: Part1.D4, J2.pin9, R2.Pin_0, Q3.gate
  N8: Part1.D5, J2.pin8, R5.Pin_0, Q4.gate
  N9: Part1.D6, J2.pin7, Q5.gate, R3.Pin_0
  N10: Part1.D7, J2.pin6
  N11: Part1.D8, J2.pin5
  N12: Part1.D9, J2.pin4
  N13: Part1.D10, J2.pin3
  N14: Part1.D11/MOSI, J2.pin2
  N15: Part1.D12/MISO, J2.pin1
  N16: Part1.VIN, J1.pin15, J6.pin2
  N17: Part1.5V, J1.pin12
  N18: Part1.A7, J1.pin11
  N19: Part1.A6, J1.pin10
  N20: Part1.A5, J1.pin9
  N21: Part1.A4, J1.pin8
  N22: Part1.A3, J1.pin7
  N23: Part1.A2, J1.pin6
  N24: Part1.A1, J1.pin5
  N25: Part1.A0, J1.pin4
  N26: Part1.AREF, J1.pin3
  N27: Part1.3V3, J1.pin2
  N28: Part1.D13/SCK, J1.pin1
  N29: LED1.anode, R1.Pin_1
  N30: LED2.anode, R2.Pin_1
  N31: LED3.anode, R4.Pin_1
  N32: LED4.anode, R5.Pin_1
  N33: LED5.anode, R3.Pin_1
  N34: Q1.drain, J5.pin1
  N35: Q2.drain, J5.pin2
  N36: Q3.drain, J5.pin3
  N37: Q4.drain, J5.pin4
  N38: Q5.drain, J5.pin5
